# Fritzing sketch relay_shield (saved by Fritzing 0.9.3b)

parts:
  Part1 = Arduino Uno (Rev3)  # not connected
  U1 = 2-Channel 5v Relay Shield [package=relay-2ch5v10a]
  BATT1 = 3xAAA Switchable Battery Pack w/Bare Wire
  JACK1 = 2.1mm Barrel Jack with Terminal Block
  NEOPIXEL1 = Neopixel Strip -- Black (30/m) [part_number=1376]  # not connected

nets:
  N1: U1.K2-In, JACK1.POS
  N2: U1.K2-On, BATT1.POS
  N3: BATT1.NEG, JACK1.NEG

custom parts:
  2-Channel 5v Relay Shield: 2 Channel 5v Relay Shield w. 2x SPD-06VDC-SD-C
  3xAAA Switchable Battery Pack w/Bare Wire: 3xAAA Switchable Battery Pack w/Bare Wire Connectors
  Neopixel Strip -- Black (30/m): These NeoPixel strips have 30 digitally-addressable pixel LEDs per meter and are very affordable and are only 12.5 mm wide, 10 mm if you remove the strip from the casing.
